# Fritzing sketch Untitled Sketch (saved by Fritzing 0.9.3b)

parts:
  8x8_LED_Modul_mit_MAX1 = 8x8 LED Modul mit MAX7219 [package=THT]
  Mod1 = Raspberry Pi Pico

nets:
  N1: 8x8_LED_Modul_mit_MAX1.VCC_Eingang, Mod1.pin_40
  N2: 8x8_LED_Modul_mit_MAX1.GND_Eingang, Mod1.pin_8
  N3: 8x8_LED_Modul_mit_MAX1.DIN_Eingang, Mod1.pin_5
  N4: 8x8_LED_Modul_mit_MAX1.CS_Eingang, Mod1.pin_7
  N5: 8x8_LED_Modul_mit_MAX1.CLK_Eingang, Mod1.pin_4

custom parts:
  Raspberry Pi Pico: Raspberry Pi Pico. Based around the RP2040 microcontroller the Pico is a low cost microcontroller device bringing Raspberry Pi quality, cost, and easy of use to the microcontroller space. Jan 2021, Split part in to two versions: tht (this one) and SMD. This one will drill holes for a .1 in header in pcb to allow plugging in the module as well as providing pads to solder the module to the top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
